# Fritzing sketch diy-modules (saved by Fritzing 0.9.3b)

parts:
  Part1 = HX711 Weighing Sensor Module
  U1 = ESP32S-HiLetgo [part_number=ESP32S-HiLetgo]
  Load_Cell1 = Load Cell - Red/white/black/green
  M1 = MT3608 Module
  M2 = TP4056 Module [part_number=HW-107]
  U2 = LIPO-1000mAh [package=lipo-1000]
  S1 = SPST Switch [package=switch-spdt-smd]

nets:
  N1: Part1.VCC, U1.3.3
  GND: Part1.GND, U1.GND, M1.pin4
  N2: Part1.DO/RX, U1.GPIO18
  N3: Part1.CK/TX, U1.GPIO19
  N4: Part1.E+, Load_Cell1.wire1
  N5: Part1.E-, Load_Cell1.wire3
  N6: Part1.A+, Load_Cell1.wire4
  N7: Part1.A-, Load_Cell1.wire2
  N8: U1.VIN, M1.pin3
  N9: M1.pin1, M2.OUT-#1
  N10: M1.pin2, S1.O
  N11: M2.BAT-, U2.-
  N12: M2.BAT+, U2.+
  N13: M2.OUT-#4, S1.P

custom parts:
  ESP32S-HiLetgo: HiLetgo ESP-WROOM-32 ESP32 ESP-32S Development Board 2.4GHz Dual-Mode WiFi + Bluetooth Dual Cores Microcontroller The ESP32 integrated with Antenna switches, RF Balun, power amplifiers, low-noise amplifiers, filters, and management modules, and the entire solution occupies the least area of PCB. 2.4 GHz Wi-Fi plus Bluetooth dual-mode chip, with TSMC Ultra-low power consumption 40nm technology,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
  Load Cell - Red/white/black/green: A rectangle load cell/weighting pressure Sensor with four wires - Red, white, black, green. Normally corresponding with E+, E-, A+, A- respectively.
  MT3608 Module: MT3608 Boost Converter Module Links: Aerosemi MT3608 2A Step Up Converter datasheet
  TP4056 Module: TP4056 Lithium Battery Charge Management Module Links: TP4056 website
